// Digital circuit computer-labled.dig as structural Verilog
module computer_labled (
  input  [12:0] progIN,
  input  reset,
  input  progLoad,
  input  start,
  input  result,
  input  clk,
  input  [7:0] M,
  input  [7:0] N,
  output valid,
  output done,
  output [7:0] \output ,
  output [7:0] out_12,
  output [7:0] out_13,
  output EQ,
  output LS,
  output GT,
  output [7:0] out_17
);

  wire _000, _001, _010, _11, and_2_out, and_11_out, and_12_out, and_14_out, checkprime, cmp,
       comparator_1_eq, comparator_2_lt, comparator_3_gt, comparator_4_eq, decodeIc_2_d, decodeIc_3_d,
       isprime_d, multiplexer_4_out, multiplexer_5_out, multiplexer_6_out, multiplexer_9_out,
       multiplexer_12_out, multiplexer_15_out, multiplexer_18_out, nor_1_out, nor_2_out, not_2_out,
       not_3_out, or_2_out, or_3_out, or_4_out, or_5_out, or_6_out, or_7_out, or_8_out, or_9_out, or_10_out,
       or_11_out, or_12_out, or_13_out, or_14_out, or_15_out, or_16_out, or_17_out, plus_storeA, q1, q2,
       stop, store_accA_accB, store_operand_accA, store_operand_accB, store_Rram;
  wire [1:0] decodeIc_4_d;
  wire [2:0] decodejump_d;
  wire [3:0] decodeIc_d;
  wire [4:0] next_op_code, op_code;
  wire [7:0] accA_lt__Pram, accA_lt__Rram, add_1_s, and_1_out, barrelshifter_1_out, dataout, div_1_q,
       div_1_r, expo0_d, expo1_d, expo2_d, expo3_d, expo4_d, expo5_d, expo6_d, expo7_d, I, k, mul_1_mul,
       multiplexer_2_out, multiplexer_3_out, multiplexer_7_out, multiplexer_8_out, multiplexer_10_out,
       multiplexer_11_out, multiplexer_13_out, multiplexer_16_out, multiplexer_17_out, multiplexer_19_out,
       next_operand, not_1_out, npc, operand, or_1_out, pow, reset_inx, sub_1_s, xor_1_out;
  wire [12:8] copy_pRAM_d2;

  ROM #(.AddrBits(3), .Bits(8)) expo7 (.A(out_13[2:0]), .sel(1'b1), .D(expo7_d));
  ROM #(.AddrBits(3), .Bits(8)) expo6 (.A(out_13[2:0]), .sel(1'b1), .D(expo6_d));
  BarrelShifter #(.Bits(8)) barrelshifter_1 (.in(out_12), .shift({1'b0, out_13[2:0]}), .out(barrelshifter_1_out));
  ROM #(.AddrBits(3), .Bits(8)) expo5 (.A(out_13[2:0]), .sel(1'b1), .D(expo5_d));
  ROM #(.AddrBits(5), .Bits(4)) decodeIc (.A(op_code), .sel(1'b1), .D(decodeIc_d));
  ROM #(.AddrBits(3), .Bits(8)) expo4 (.A(out_13[2:0]), .sel(1'b1), .D(expo4_d));
  assign xor_1_out = out_13 ^ out_12;  // XOr xor_1, 8 bits wide
  ROM #(.AddrBits(3), .Bits(8)) expo3 (.A(out_13[2:0]), .sel(1'b1), .D(expo3_d));
  assign or_1_out = out_13 | out_12;  // Or or_1, 8 bits wide
  ROM #(.AddrBits(3), .Bits(8)) expo2 (.A(out_13[2:0]), .sel(1'b1), .D(expo2_d));
  Multiplexer #(.Selector_Bits(3), .Bits(8)) multiplexer_1 (
    .sel(out_12[2:0]), .in_0(expo0_d), .in_1(expo1_d), .in_2(expo2_d), .in_3(expo3_d), .in_4(expo4_d),
    .in_5(expo5_d), .in_6(expo6_d), .in_7(expo7_d), .out(pow));
  assign and_1_out = out_13 & out_12;  // And and_1, 8 bits wide
  assign not_1_out = ~out_12;  // Not not_1, 8 bits wide
  ROM #(.AddrBits(5)) decodeIc_2 (.A(op_code), .sel(1'b1), .D(decodeIc_2_d));
  ROM #(.AddrBits(3), .Bits(8)) expo1 (.A(out_13[2:0]), .sel(1'b1), .D(expo1_d));
  Sub #(.Bits(8)) sub_1 (.a(out_12), .b(out_13), .c_i(1'b0), .s(sub_1_s));  // open: c_o
  Mul #(.Bits(4)) mul_1 (.a(out_12[3:0]), .b(out_13[3:0]), .mul(mul_1_mul));
  Div #(.Bits(8)) div_1 (.a(out_12), .b(out_13), .q(div_1_q), .r(div_1_r));
  or or_2 (or_2_out, reset, decodeIc_2_d);
  Add #(.Bits(8)) add_1 (.a(out_12), .b(out_13), .c_i(1'b0), .s(add_1_s));  // open: c_o
  Register #(.Bits(8)) register_1 (.D(multiplexer_3_out), .C(clk), .en(or_2_out), .Q(out_12));
  ROM #(.AddrBits(3), .Bits(8)) expo0 (.A(out_13[2:0]), .sel(1'b1), .D(expo0_d));
  Multiplexer #(.Selector_Bits(4), .Bits(8)) multiplexer_2 (
    .sel(decodeIc_d), .in_0(operand), .in_1(out_13), .in_2(out_17), .in_3(accA_lt__Pram),
    .in_4(accA_lt__Rram), .in_5(add_1_s), .in_6(sub_1_s), .in_7(mul_1_mul), .in_8(div_1_q), .in_9(div_1_r),
    .in_10(pow), .in_11(not_1_out), .in_12(and_1_out), .in_13(or_1_out), .in_14(xor_1_out),
    .in_15(barrelshifter_1_out), .out(multiplexer_2_out));
  Multiplexer #(.Bits(8)) multiplexer_3 (
    .sel(reset), .in_0(multiplexer_2_out), .in_1({8{1'b0}}), .out(multiplexer_3_out));
  Comparator #(.Bits(8)) comparator_1 (.a(out_12), .b(out_13), .eq(comparator_1_eq));  // open: gt, lt
  Comparator #(.Bits(8)) comparator_2 (.a(out_12), .b(out_13), .lt(comparator_2_lt));  // open: gt, eq
  Comparator #(.Bits(8)) comparator_3 (.a(out_12), .b(out_13), .gt(comparator_3_gt));  // open: eq, lt
  or or_3 (or_3_out, store_accA_accB, reset, store_operand_accB);
  ROM #(.AddrBits(8)) isprime (.A(out_12), .sel(1'b1), .D(isprime_d));
  Multiplexer multiplexer_4 (.sel(reset), .in_0(comparator_1_eq), .in_1(1'b0), .out(multiplexer_4_out));
  Multiplexer multiplexer_5 (.sel(or_4_out), .in_0(comparator_2_lt), .in_1(1'b0), .out(multiplexer_5_out));
  Multiplexer multiplexer_6 (.sel(or_4_out), .in_0(comparator_3_gt), .in_1(1'b0), .out(multiplexer_6_out));
  or or_4 (or_4_out, reset, start);
  Multiplexer #(.Bits(8)) multiplexer_7 (.sel(store_accA_accB), .in_0(operand), .in_1(out_12), .out(multiplexer_7_out));
  Multiplexer #(.Bits(8)) multiplexer_8 (
    .sel(reset), .in_0(multiplexer_7_out), .in_1({8{1'b0}}), .out(multiplexer_8_out));
  Register #(.Bits(8)) register_2 (.D(multiplexer_8_out), .C(clk), .en(or_3_out), .Q(out_13));
  Multiplexer multiplexer_9 (.sel(cmp), .in_0(isprime_d), .in_1(multiplexer_4_out), .out(multiplexer_9_out));
  Register register_3 (.D(multiplexer_9_out), .C(clk), .en(or_7_out), .Q(EQ));
  Register register_4 (.D(multiplexer_5_out), .C(clk), .en(or_5_out), .Q(LS));
  Register register_5 (.D(multiplexer_6_out), .C(clk), .en(or_6_out), .Q(GT));
  or or_5 (or_5_out, reset, cmp, start);
  or or_6 (or_6_out, reset, cmp, start);
  ROM #(.AddrBits(5)) decodeIc_3 (.A(op_code), .sel(1'b1), .D(decodeIc_3_d));
  or or_7 (or_7_out, cmp, reset, start, checkprime);
  ROM #(.AddrBits(5), .Bits(2)) decodeIc_4 (.A(op_code), .sel(1'b1), .D(decodeIc_4_d));
  or or_8 (or_8_out, reset, decodeIc_3_d);
  Multiplexer #(.Bits(8)) multiplexer_10 (
    .sel(reset), .in_0(multiplexer_11_out), .in_1({8{1'b0}}), .out(multiplexer_10_out));
  Register #(.Bits(8)) register_6 (.D(multiplexer_10_out), .C(clk), .en(or_8_out), .Q(out_17));
  Multiplexer #(.Selector_Bits(2), .Bits(8)) multiplexer_11 (
    .sel(decodeIc_4_d), .in_0(out_12), .in_1(M), .in_2(N), .in_3({8{1'b0}}), .out(multiplexer_11_out));
  Add #(.Bits(8)) add_2 (.a(I), .b({8{1'b0}}), .c_i(1'b1), .s(npc));  // open: c_o
  CounterPreset #(.maxValue(16), .Bits(8)) counterpreset_1 (
    .en(reset), .C(clk), .dir(1'b0), .in({8{1'b0}}), .ld(1'b0), .clr(~reset), .out(reset_inx));  // open: ovf
  or or_9 (or_9_out, EQ, GT);
  ROM #(.AddrBits(5), .Bits(3)) decodejump (.A(op_code), .sel(1'b1), .D(decodejump_d));
  Multiplexer #(.Selector_Bits(3)) multiplexer_12 (
    .sel(decodejump_d), .in_0(1'b0), .in_1(1'b1), .in_2(EQ), .in_3(GT), .in_4(LS), .in_5(or_9_out),
    .in_6(1'b0), .in_7(1'b0), .out(multiplexer_12_out));
  and and_2 (and_2_out, _11, ~done);  // And
  or or_10 (or_10_out, start, _010, reset, result);
  or or_11 (or_11_out, _001, progLoad);
  or or_12 (or_12_out, start, reset);
  and and_3 (stop, op_code[0], op_code[1], op_code[2], op_code[3], op_code[4]);
  and and_4 (plus_storeA, op_code[0], ~op_code[1], ~op_code[2], ~op_code[3], op_code[4]);  // And
  and and_5 (store_Rram, op_code[0], op_code[1], ~op_code[2], op_code[3], ~op_code[4]);  // And
  and and_6 (store_operand_accA, op_code[0], ~op_code[1], ~op_code[2], ~op_code[3], ~op_code[4]);  // And
  and and_7 (store_operand_accB, ~op_code[0], op_code[1], ~op_code[2], ~op_code[3], ~op_code[4]);  // And
  and and_8 (store_accA_accB, ~op_code[0], ~op_code[1], op_code[2], ~op_code[3], ~op_code[4]);  // And
  and and_9 (cmp, op_code[0], op_code[1], op_code[2], ~op_code[3], op_code[4]);  // And
  and and_10 (checkprime, op_code[0], ~op_code[1], op_code[2], op_code[3], op_code[4]);  // And
  CounterPreset #(.maxValue(16), .Bits(8)) counterpreset_2 (
    .en(and_2_out), .C(clk), .dir(1'b0), .in(next_operand), .ld(store_Rram), .clr(or_10_out), .out(k));  // open: ovf
  CounterPreset #(.maxValue(255), .Bits(8)) counterpreset_3 (
    .en(or_11_out), .C(clk), .dir(1'b0), .in(operand), .ld(multiplexer_12_out), .clr(or_12_out), .out(I));  // open: ovf
  Multiplexer #(.Bits(8)) multiplexer_13 (.sel(_001), .in_0(I), .in_1(npc), .out(multiplexer_13_out));
  and and_11 (and_11_out, stop, ~reset);  // And
  nor nor_1 (nor_1_out, start, reset);
  Multiplexer #(.Bits(8)) multiplexer_14 (.sel(or_13_out), .in_0({8{1'b0}}), .in_1(dataout), .out(\output ));
  or or_13 (or_13_out, and_12_out, _11);
  and and_12 (and_12_out, result, clk);
  not not_2 (not_2_out, reset);
  RAMDualAccess #(.AddrBits(8), .Bits(13)) pRAM (
    .str(progLoad), .C(clk), .ld(1'b1), .A1(I), .Din1(progIN), .A2(I), .D1({op_code, operand}));  // open: D2
  Multiplexer #(.Selector_Bits(2)) multiplexer_15 (
    .sel({q2, q1}), .in_0(1'b0), .in_1(and_11_out), .in_2(not_2_out), .in_3(nor_1_out),
    .out(multiplexer_15_out));
  Seven_Seg_Hex seven_seg_hex_1 (.d(\output [7:4]), .dp(1'b0));
  Comparator #(.Bits(8)) comparator_4 (.a(k), .b(8'h10), .eq(comparator_4_eq));  // open: gt, lt
  or or_14 (or_14_out, _000, _11);
  RAMDualAccess #(.AddrBits(8), .Bits(13)) copy_pRAM (
    .str(progLoad), .C(clk), .ld(1'b1), .A1(multiplexer_13_out), .Din1(progIN), .A2(operand),
    .D1({next_op_code, next_operand}), .D2({copy_pRAM_d2, accA_lt__Pram}));
  D_FF d_ff_1 (.D(multiplexer_15_out), .C(~clk), .Q(q2));  // open: nQ
  Seven_Seg_Hex seven_seg_hex_2 (.d(\output [3:0]), .dp(1'b0));
  and and_13 (done, comparator_4_eq, or_14_out);
  Multiplexer #(.Bits(8)) multiplexer_16 (.sel(store_Rram), .in_0(k), .in_1(operand), .out(multiplexer_16_out));
  and and_14 (and_14_out, result, ~reset);  // And
  not not_3 (not_3_out, stop);
  nor nor_2 (nor_2_out, start, reset);
  or or_15 (or_15_out, _11, _010);
  or or_16 (or_16_out, store_Rram, reset);
  Multiplexer #(.Bits(8)) multiplexer_17 (
    .sel(reset), .in_0(multiplexer_16_out), .in_1(reset_inx), .out(multiplexer_17_out));
  Multiplexer #(.Selector_Bits(2)) multiplexer_18 (
    .sel({q2, q1}), .in_0(start), .in_1(not_3_out), .in_2(and_14_out), .in_3(nor_2_out),
    .out(multiplexer_18_out));
  and and_15 (valid, or_15_out, ~reset);  // And
  Multiplexer #(.Bits(8)) multiplexer_19 (.sel(reset), .in_0(out_12), .in_1({8{1'b0}}), .out(multiplexer_19_out));
  or or_17 (or_17_out, result, _11);
  D_FF d_ff_2 (.D(multiplexer_18_out), .C(~clk), .Q(q1));  // open: nQ
  RAMDualAccess #(.AddrBits(8), .Bits(8)) rRAM (
    .str(or_16_out), .C(clk), .ld(or_17_out), .A1(multiplexer_17_out), .Din1(multiplexer_19_out),
    .A2(operand), .D1(dataout), .D2(accA_lt__Rram));
  Demultiplexer #(.Selector_Bits(2)) demultiplexer_1 (
    .sel({q2, q1}), .in(1'b1), .out_0(_000), .out_1(_001), .out_2(_010), .out_3(_11));

  // Other names for the same wires on the sheet: accA[7:0] = out_12; accB[7:0] = out_13; regC[7:0] = out_17

  // Notes on the sheet:
  //   register - ALU
  //   ALU
  //   contents of expo7 (hex, n*v repeats v):
  //   1,7,31,157,961,41a7,1cb91,c90f7
  //   contents of expo6 (hex, n*v repeats v):
  //   1,6,24,d8,510,1e60,b640,44580
  //   contents of expo5 (hex, n*v repeats v):
  //   1,5,19,7d,271,c35,3d09,1312d
  //   contents of decodeIc (hex, n*v repeats v):
  //   0,0,0,1,0,0,2,0,0,3,4,6*0,5,6,7,8,9,a,0,b,c,d,e,f
  //   contents of expo4 (hex, n*v repeats v):
  //   1,4,10,40,100,400,1000,4000
  //   For accumulator A
  //   contents of expo3 (hex, n*v repeats v):
  //   1,3,9,1b,51,f3,2d9,88b
  //   contents of expo2 (hex, n*v repeats v):
  //   1,2,4,8,10,20,40,80
  //   contents of decodeIc_2 (hex, n*v repeats v):
  //   0,1,0,1,0,0,1,0,0,3,1,6*0,5,1,7,1,9,1,0,b,1,d,1,f
  //   contents of expo1 (hex, n*v repeats v):
  //   8*1
  //   contents of expo0 (hex, n*v repeats v):
  //   1
  //   For accumulator B
  //   register flag
  //   contents of isprime (hex, n*v repeats v):
  //   0,0,1,1,0,1,0,1,0,0,0,1,0,1,0,0,0,1,0,1,0,0,0,1,0,1,0,0,0,1,0
  //   ,1,0,0,0,1,0,1,0,0,0,1,0,1,0,0,0,1,5*0,1,5*0,1,0,1,5*0,1,0,0,0
  //   ,1,0,1,5*0,1,0,0,0,1,5*0,1,7*0,1,0,0,0,1,0,1,0,0,0,1,0,1,0,0,0
  //   ,1,13*0,1,0,0,0,1,5*0,1,0,1,9*0,1,0,1,5*0,1,5*0,1,0,0,0,1,5*0
  //   ,1,5*0,1,0,1,9*0,1,0,1,0,0,0,1,0,1,11*0,1,11*0,1,0,0,0,1,0,1,0,0,0
  //   ,1,5*0,1,0,1,9*0,1
  //   For register C
  //   contents of decodeIc_3 (hex, n*v repeats v):
  //   5*0,1,0,1,1,0,4,9*0,8,4*0,c
  //   contents of decodeIc_4 (hex, n*v repeats v):
  //   7*0,1,2,0,4,9*0,8,4*0,c
  //   Counter
  //   input
  //   contents of decodejump (hex, n*v repeats v):
  //   12*0,1,2,3,4,5
  //   Some decode op-code
  //   RAM
  //   state machie - control unit
  //   display - output
endmodule

/* Test case 01_P01T01:
M N progIN reset progLoad start result clk valid done output
0 0 0 0 0 0 0 0 x x x
0 0 0 0 0 0 0 1 x x x
0 0 0 1 0 0 0 0 x x x
0 0 0 1 0 0 0 1 0 0 0
0 0 0 0 0 0 0 0 0 0 0
0 0 0 0 0 0 0 1 0 0 0
0 0 0 0 0 0 0 0 0 0 0
0 0 0 0 0 0 0 1 0 0 0
0 0 0 0 0 0 0 0 0 0 0
0 0 0 0 0 0 0 1 0 0 0
0 0 0 0 0 0 0 0 0 0 0
0 0 0 0 0 0 0 1 0 0 0
0 0 0 0 0 0 0 0 0 0 0
0 0 0 0 0 0 0 1 0 0 0
0 0 0 0 0 0 0 0 0 0 0
0 0 0 0 0 0 0 1 0 0 0
0 0 0 0 0 0 0 0 0 0 0
0 0 0 0 0 0 0 1 0 0 0
0 0 0 0 0 0 0 0 0 0 0
0 0 0 0 0 0 0 1 0 0 0
0 0 0 0 0 0 0 0 0 0 0
0 0 0 0 0 0 0 1 0 0 0
0 0 0 0 0 0 0 0 0 0 0
0 0 0 0 0 0 0 1 0 0 0
0 0 0 0 0 0 0 0 0 0 0
0 0 0 0 0 0 0 1 0 0 0
0 0 0 0 0 0 0 0 0 0 0
0 0 0 0 0 0 0 1 0 0 0
0 0 0 0 0 0 0 0 0 0 0
0 0 0 0 0 0 0 1 0 0 0
0 0 0 0 0 0 0 0 0 0 0
0 0 0 0 0 0 0 1 0 0 0
0 0 0 0 0 0 0 0 0 0 0
0 0 0 0 0 0 0 1 0 0 0
0 0 0 0 0 0 0 0 0 0 0
0 0 0 0 0 0 0 1 0 0 0
0 0 0 0 0 0 0 0 0 0 0
0 0 0 0 0 0 0 1 0 0 0
0 0 0 0 0 0 0 0 0 0 0
0 0 0 0 0 0 0 1 0 0 0
0 0 0 0 0 0 0 0 0 0 0
0 0 0 0 0 0 0 1 0 0 0
0 0 271 0 1 0 0 0 0 0 0
0 0 271 0 1 0 0 1 0 0 0
0 0 565 0 1 0 0 0 0 0 0
0 0 565 0 1 0 0 1 0 0 0
0 0 4352 0 1 0 0 0 0 0 0
0 0 4352 0 1 0 0 1 0 0 0
0 0 2819 0 1 0 0 0 0 0 0
0 0 2819 0 1 0 0 1 0 0 0
0 0 7936 0 1 0 0 0 0 0 0
0 0 7936 0 1 0 0 1 0 0 0
0 0 0 0 0 1 0 0 0 0 0
0 0 0 0 0 1 0 1 0 0 0
0 0 0 0 0 0 0 0 x 0 0
0 0 0 0 0 0 0 1 x 0 0
0 0 0 0 0 0 0 0 x 0 0
0 0 0 0 0 0 0 1 x 0 0
0 0 0 0 0 0 0 0 x 0 0
0 0 0 0 0 0 0 1 x 0 0
0 0 0 0 0 0 0 0 x 0 0
0 0 0 0 0 0 0 1 x 0 0
0 0 0 0 0 0 0 0 x 0 0
0 0 0 0 0 0 0 1 x 0 0
0 0 0 0 0 0 0 0 x 0 0
0 0 0 0 0 0 0 1 x 0 0
0 0 0 0 0 0 0 0 x 0 0
0 0 0 0 0 0 0 1 x 0 0
0 0 0 0 0 0 0 0 x 0 0
0 0 0 0 0 0 0 1 x 0 0
0 0 0 0 0 0 0 0 x 0 0
0 0 0 0 0 0 0 1 x 0 0
0 0 0 0 0 0 0 0 x 0 0
0 0 0 0 0 0 0 1 x 0 0
0 0 0 0 0 0 0 0 x 0 0
0 0 0 0 0 0 0 1 x 0 0
0 0 0 0 0 0 0 0 x 0 0
0 0 0 0 0 0 0 1 x 0 0
0 0 0 0 0 0 0 0 x 0 0
0 0 0 0 0 0 0 1 x 0 0
0 0 0 0 0 0 0 0 x 0 0
0 0 0 0 0 0 0 1 x 0 0
0 0 0 0 0 0 0 0 x 0 0
0 0 0 0 0 0 0 1 x 0 0
0 0 0 0 0 0 0 0 x 0 0
0 0 0 0 0 0 0 1 x 0 0
0 0 0 0 0 0 0 0 x 0 0
0 0 0 0 0 0 0 1 x 0 0
0 0 0 0 0 0 0 0 x 0 0
0 0 0 0 0 0 0 1 x 0 0
0 0 0 0 0 0 0 0 x 0 0
0 0 0 0 0 0 0 1 x 0 0
0 0 0 0 0 0 0 0 x 0 0
0 0 0 0 0 0 0 1 x 0 0
0 0 0 0 0 0 0 0 x 0 0
0 0 0 0 0 0 0 1 x 0 0
0 0 0 0 0 0 0 0 x 0 0
0 0 0 0 0 0 0 1 x 0 0
0 0 0 0 0 0 0 0 x 0 0
0 0 0 0 0 0 0 1 x 0 0
0 0 0 0 0 0 0 0 x 0 0
0 0 0 0 0 0 0 1 x 0 0
0 0 0 0 0 0 0 0 x 0 0
0 0 0 0 0 0 0 1 x 0 0
0 0 0 0 0 0 0 0 x 0 0
0 0 0 0 0 0 0 1 1 0 0
0 0 0 0 0 0 1 0 1 0 0
0 0 0 0 0 0 1 1 1 0 0
0 0 0 0 0 0 0 0 1 0 0
0 0 0 0 0 0 0 1 1 0 0
0 0 0 0 0 0 0 0 1 0 0
0 0 0 0 0 0 0 1 1 0 0
0 0 0 0 0 0 0 0 1 0 0
0 0 0 0 0 0 0 1 1 0 68
0 0 0 0 0 0 0 0 1 0 68
0 0 0 0 0 0 0 1 1 0 0
0 0 0 0 0 0 0 0 1 0 0
0 0 0 0 0 0 0 1 1 0 0
0 0 0 0 0 0 0 0 1 0 0
0 0 0 0 0 0 0 1 1 0 0
0 0 0 0 0 0 0 0 1 0 0
0 0 0 0 0 0 0 1 1 0 0
0 0 0 0 0 0 0 0 1 0 0
0 0 0 0 0 0 0 1 1 0 0
0 0 0 0 0 0 0 0 1 0 0
0 0 0 0 0 0 0 1 1 0 0
0 0 0 0 0 0 0 0 1 0 0
0 0 0 0 0 0 0 1 1 0 0
0 0 0 0 0 0 0 0 1 0 0
0 0 0 0 0 0 0 1 1 0 0
0 0 0 0 0 0 0 0 1 0 0
0 0 0 0 0 0 0 1 1 0 0
0 0 0 0 0 0 0 0 1 0 0
0 0 0 0 0 0 0 1 1 0 0
0 0 0 0 0 0 0 0 1 0 0
0 0 0 0 0 0 0 1 1 0 0
0 0 0 0 0 0 0 0 1 0 0
0 0 0 0 0 0 0 1 1 0 0
0 0 0 0 0 0 0 0 1 0 0
0 0 0 0 0 0 0 1 1 1 0
0 0 0 0 0 0 0 0 1 1 0
0 0 0 0 0 0 0 1 1 1 0
0 0 0 0 0 0 0 0 1 1 0
*/

/* Test case 03_P02T01:
M N progIN reset progLoad start result clk valid done output
0 0 0 0 0 0 0 0 x x x
0 0 0 0 0 0 0 1 x x x
0 0 0 1 0 0 0 0 x x x
0 0 0 1 0 0 0 1 0 0 0
0 0 0 0 0 0 0 0 0 0 0
0 0 0 0 0 0 0 1 0 0 0
0 0 0 0 0 0 0 0 0 0 0
0 0 0 0 0 0 0 1 0 0 0
0 0 0 0 0 0 0 0 0 0 0
0 0 0 0 0 0 0 1 0 0 0
0 0 0 0 0 0 0 0 0 0 0
0 0 0 0 0 0 0 1 0 0 0
0 0 0 0 0 0 0 0 0 0 0
0 0 0 0 0 0 0 1 0 0 0
0 0 0 0 0 0 0 0 0 0 0
0 0 0 0 0 0 0 1 0 0 0
0 0 0 0 0 0 0 0 0 0 0
0 0 0 0 0 0 0 1 0 0 0
0 0 0 0 0 0 0 0 0 0 0
0 0 0 0 0 0 0 1 0 0 0
0 0 0 0 0 0 0 0 0 0 0
0 0 0 0 0 0 0 1 0 0 0
0 0 0 0 0 0 0 0 0 0 0
0 0 0 0 0 0 0 1 0 0 0
0 0 0 0 0 0 0 0 0 0 0
0 0 0 0 0 0 0 1 0 0 0
0 0 0 0 0 0 0 0 0 0 0
0 0 0 0 0 0 0 1 0 0 0
0 0 0 0 0 0 0 0 0 0 0
0 0 0 0 0 0 0 1 0 0 0
0 0 0 0 0 0 0 0 0 0 0
0 0 0 0 0 0 0 1 0 0 0
0 0 0 0 0 0 0 0 0 0 0
0 0 0 0 0 0 0 1 0 0 0
0 0 0 0 0 0 0 0 0 0 0
0 0 0 0 0 0 0 1 0 0 0
0 0 0 0 0 0 0 0 0 0 0
0 0 0 0 0 0 0 1 0 0 0
0 0 0 0 0 0 0 0 0 0 0
0 0 0 0 0 0 0 1 0 0 0
0 0 0 0 0 0 0 0 0 0 0
0 0 0 0 0 0 0 1 0 0 0
0 0 271 0 1 0 0 0 0 0 0
0 0 271 0 1 0 0 1 0 0 0
0 0 566 0 1 0 0 0 0 0 0
0 0 566 0 1 0 0 1 0 0 0
0 0 5888 0 1 0 0 0 0 0 0
0 0 5888 0 1 0 0 1 0 0 0
0 0 3599 0 1 0 0 0 0 0 0
0 0 3599 0 1 0 0 1 0 0 0
0 0 4110 0 1 0 0 0 0 0 0
0 0 4110 0 1 0 0 1 0 0 0
0 0 3856 0 1 0 0 0 0 0 0
0 0 3856 0 1 0 0 1 0 0 0
0 0 0 0 1 0 0 0 0 0 0
0 0 0 0 1 0 0 1 0 0 0
0 0 0 0 1 0 0 0 0 0 0
0 0 0 0 1 0 0 1 0 0 0
0 0 0 0 1 0 0 0 0 0 0
0 0 0 0 1 0 0 1 0 0 0
0 0 0 0 1 0 0 0 0 0 0
0 0 0 0 1 0 0 1 0 0 0
0 0 0 0 1 0 0 0 0 0 0
0 0 0 0 1 0 0 1 0 0 0
0 0 0 0 1 0 0 0 0 0 0
0 0 0 0 1 0 0 1 0 0 0
0 0 0 0 1 0 0 0 0 0 0
0 0 0 0 1 0 0 1 0 0 0
0 0 0 0 1 0 0 0 0 0 0
0 0 0 0 1 0 0 1 0 0 0
0 0 0 0 1 0 0 0 0 0 0
0 0 0 0 1 0 0 1 0 0 0
0 0 0 0 1 0 0 0 0 0 0
0 0 0 0 1 0 0 1 0 0 0
0 0 4352 0 1 0 0 0 0 0 0
0 0 4352 0 1 0 0 1 0 0 0
0 0 2819 0 1 0 0 0 0 0 0
0 0 2819 0 1 0 0 1 0 0 0
0 0 7936 0 1 0 0 0 0 0 0
0 0 7936 0 1 0 0 1 0 0 0
0 0 0 0 1 0 0 0 0 0 0
0 0 0 0 1 0 0 1 0 0 0
0 0 0 0 0 0 0 0 0 0 0
0 0 0 0 0 0 0 1 0 0 0
0 0 0 0 0 0 0 0 0 0 0
0 0 0 0 0 0 0 1 0 0 0
0 0 0 0 0 0 0 0 0 0 0
0 0 0 0 0 0 0 1 0 0 0
0 0 0 0 0 1 0 0 0 0 0
0 0 0 0 0 1 0 1 0 0 0
0 0 0 0 0 0 0 0 x 0 0
0 0 0 0 0 0 0 1 x 0 0
0 0 0 0 0 0 0 0 x 0 0
0 0 0 0 0 0 0 1 x 0 0
0 0 0 0 0 0 0 0 x 0 0
0 0 0 0 0 0 0 1 x 0 0
0 0 0 0 0 0 0 0 x 0 0
0 0 0 0 0 0 0 1 x 0 0
0 0 0 0 0 0 0 0 x 0 0
0 0 0 0 0 0 0 1 x 0 0
0 0 0 0 0 0 0 0 x 0 0
0 0 0 0 0 0 0 1 x 0 0
0 0 0 0 0 0 0 0 x 0 0
0 0 0 0 0 0 0 1 x 0 0
0 0 0 0 0 0 0 0 x 0 0
0 0 0 0 0 0 0 1 x 0 0
0 0 0 0 0 0 0 0 x 0 0
0 0 0 0 0 0 0 1 x 0 0
0 0 0 0 0 0 0 0 x 0 0
0 0 0 0 0 0 0 1 x 0 0
0 0 0 0 0 0 0 0 x 0 0
0 0 0 0 0 0 0 1 x 0 0
0 0 0 0 0 0 0 0 x 0 0
0 0 0 0 0 0 0 1 x 0 0
0 0 0 0 0 0 0 0 x 0 0
0 0 0 0 0 0 0 1 x 0 0
0 0 0 0 0 0 0 0 x 0 0
0 0 0 0 0 0 0 1 x 0 0
0 0 0 0 0 0 0 0 x 0 0
0 0 0 0 0 0 0 1 x 0 0
0 0 0 0 0 0 0 0 x 0 0
0 0 0 0 0 0 0 1 x 0 0
0 0 0 0 0 0 0 0 x 0 0
0 0 0 0 0 0 0 1 x 0 0
0 0 0 0 0 0 0 0 x 0 0
0 0 0 0 0 0 0 1 x 0 0
0 0 0 0 0 0 0 0 x 0 0
0 0 0 0 0 0 0 1 x 0 0
0 0 0 0 0 0 0 0 x 0 0
0 0 0 0 0 0 0 1 x 0 0
0 0 0 0 0 0 0 0 x 0 0
0 0 0 0 0 0 0 1 x 0 0
0 0 0 0 0 0 0 0 x 0 0
0 0 0 0 0 0 0 1 x 0 0
0 0 0 0 0 0 0 0 x 0 0
0 0 0 0 0 0 0 1 x 0 0
0 0 0 0 0 0 0 0 x 0 0
0 0 0 0 0 0 0 1 x 0 0
0 0 0 0 0 0 0 0 x 0 0
0 0 0 0 0 0 0 1 x 0 0
0 0 0 0 0 0 0 0 x 0 0
0 0 0 0 0 0 0 1 1 0 0
0 0 0 0 0 0 1 0 1 0 0
0 0 0 0 0 0 1 1 1 0 0
0 0 0 0 0 0 0 0 1 0 0
0 0 0 0 0 0 0 1 1 0 0
0 0 0 0 0 0 0 0 1 0 0
0 0 0 0 0 0 0 1 1 0 0
0 0 0 0 0 0 0 0 1 0 0
0 0 0 0 0 0 0 1 1 0 69
0 0 0 0 0 0 0 0 1 0 69
0 0 0 0 0 0 0 1 1 0 0
0 0 0 0 0 0 0 0 1 0 0
0 0 0 0 0 0 0 1 1 0 0
0 0 0 0 0 0 0 0 1 0 0
0 0 0 0 0 0 0 1 1 0 0
0 0 0 0 0 0 0 0 1 0 0
0 0 0 0 0 0 0 1 1 0 0
0 0 0 0 0 0 0 0 1 0 0
0 0 0 0 0 0 0 1 1 0 0
0 0 0 0 0 0 0 0 1 0 0
0 0 0 0 0 0 0 1 1 0 0
0 0 0 0 0 0 0 0 1 0 0
0 0 0 0 0 0 0 1 1 0 0
0 0 0 0 0 0 0 0 1 0 0
0 0 0 0 0 0 0 1 1 0 0
0 0 0 0 0 0 0 0 1 0 0
0 0 0 0 0 0 0 1 1 0 0
0 0 0 0 0 0 0 0 1 0 0
0 0 0 0 0 0 0 1 1 0 0
0 0 0 0 0 0 0 0 1 0 0
0 0 0 0 0 0 0 1 1 0 0
0 0 0 0 0 0 0 0 1 0 0
0 0 0 0 0 0 0 1 1 0 0
0 0 0 0 0 0 0 0 1 0 0
0 0 0 0 0 0 0 1 1 1 0
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*/

/* Test case 05_P04T01:
M N progIN reset progLoad start result clk valid done output
0 0 0 0 0 0 0 0 x x x
0 0 0 0 0 0 0 1 x x x
0 0 0 1 0 0 0 0 x x x
0 0 0 1 0 0 0 1 0 0 0
0 0 0 0 0 0 0 0 0 0 0
0 0 0 0 0 0 0 1 0 0 0
0 0 0 0 0 0 0 0 0 0 0
0 0 0 0 0 0 0 1 0 0 0
0 0 0 0 0 0 0 0 0 0 0
0 0 0 0 0 0 0 1 0 0 0
0 0 0 0 0 0 0 0 0 0 0
0 0 0 0 0 0 0 1 0 0 0
0 0 0 0 0 0 0 0 0 0 0
0 0 0 0 0 0 0 1 0 0 0
0 0 0 0 0 0 0 0 0 0 0
0 0 0 0 0 0 0 1 0 0 0
0 0 0 0 0 0 0 0 0 0 0
0 0 0 0 0 0 0 1 0 0 0
0 0 0 0 0 0 0 0 0 0 0
0 0 0 0 0 0 0 1 0 0 0
0 0 0 0 0 0 0 0 0 0 0
0 0 0 0 0 0 0 1 0 0 0
0 0 0 0 0 0 0 0 0 0 0
0 0 0 0 0 0 0 1 0 0 0
0 0 0 0 0 0 0 0 0 0 0
0 0 0 0 0 0 0 1 0 0 0
0 0 0 0 0 0 0 0 0 0 0
0 0 0 0 0 0 0 1 0 0 0
0 0 0 0 0 0 0 0 0 0 0
0 0 0 0 0 0 0 1 0 0 0
0 0 0 0 0 0 0 0 0 0 0
0 0 0 0 0 0 0 1 0 0 0
0 0 0 0 0 0 0 0 0 0 0
0 0 0 0 0 0 0 1 0 0 0
0 0 0 0 0 0 0 0 0 0 0
0 0 0 0 0 0 0 1 0 0 0
0 0 0 0 0 0 0 0 0 0 0
0 0 0 0 0 0 0 1 0 0 0
0 0 0 0 0 0 0 0 0 0 0
0 0 0 0 0 0 0 1 0 0 0
0 0 0 0 0 0 0 0 0 0 0
0 0 0 0 0 0 0 1 0 0 0
0 0 0 0 0 0 0 0 0 0 0
0 0 0 0 0 0 0 1 0 0 0
0 0 271 0 1 0 0 0 0 0 0
0 0 271 0 1 0 0 1 0 0 0
0 0 7424 0 1 0 0 0 0 0 0
0 0 7424 0 1 0 0 1 0 0 0
0 0 3328 0 1 0 0 0 0 0 0
0 0 3328 0 1 0 0 1 0 0 0
0 0 257 0 1 0 0 0 0 0 0
0 0 257 0 1 0 0 1 0 0 0
0 0 3331 0 1 0 0 0 0 0 0
0 0 3331 0 1 0 0 1 0 0 0
0 0 455 0 1 0 0 0 0 0 0
0 0 455 0 1 0 0 1 0 0 0
0 0 7424 0 1 0 0 0 0 0 0
0 0 7424 0 1 0 0 1 0 0 0
0 0 3337 0 1 0 0 0 0 0 0
0 0 3337 0 1 0 0 1 0 0 0
0 0 2818 0 1 0 0 0 0 0 0
0 0 2818 0 1 0 0 1 0 0 0
0 0 2819 0 1 0 0 0 0 0 0
0 0 2819 0 1 0 0 1 0 0 0
0 0 7936 0 1 0 0 0 0 0 0
0 0 7936 0 1 0 0 1 0 0 0
0 0 0 0 0 0 0 0 0 0 0
0 0 0 0 0 0 0 1 0 0 0
0 0 0 0 0 0 0 0 0 0 0
0 0 0 0 0 0 0 1 0 0 0
0 0 0 0 0 0 0 0 0 0 0
0 0 0 0 0 0 0 1 0 0 0
0 0 0 0 0 1 0 0 0 0 0
0 0 0 0 0 1 0 1 0 0 0
0 0 0 0 0 0 0 0 x 0 0
0 0 0 0 0 0 0 1 x 0 0
0 0 0 0 0 0 0 0 x 0 0
0 0 0 0 0 0 0 1 x 0 0
0 0 0 0 0 0 0 0 x 0 0
0 0 0 0 0 0 0 1 x 0 0
0 0 0 0 0 0 0 0 x 0 0
0 0 0 0 0 0 0 1 x 0 0
0 0 0 0 0 0 0 0 x 0 0
0 0 0 0 0 0 0 1 x 0 0
0 0 0 0 0 0 0 0 x 0 0
0 0 0 0 0 0 0 1 x 0 0
0 0 0 0 0 0 0 0 x 0 0
0 0 0 0 0 0 0 1 x 0 0
0 0 0 0 0 0 0 0 x 0 0
0 0 0 0 0 0 0 1 x 0 0
0 0 0 0 0 0 0 0 x 0 0
0 0 0 0 0 0 0 1 x 0 0
0 0 0 0 0 0 0 0 x 0 0
0 0 0 0 0 0 0 1 x 0 0
0 0 0 0 0 0 0 0 x 0 0
0 0 0 0 0 0 0 1 x 0 0
0 0 0 0 0 0 0 0 x 0 0
0 0 0 0 0 0 0 1 x 0 0
0 0 0 0 0 0 0 0 x 0 0
0 0 0 0 0 0 0 1 x 0 0
0 0 0 0 0 0 0 0 x 0 0
0 0 0 0 0 0 0 1 x 0 0
0 0 0 0 0 0 0 0 x 0 0
0 0 0 0 0 0 0 1 x 0 0
0 0 0 0 0 0 0 0 x 0 0
0 0 0 0 0 0 0 1 x 0 0
0 0 0 0 0 0 0 0 x 0 0
0 0 0 0 0 0 0 1 x 0 0
0 0 0 0 0 0 0 0 x 0 0
0 0 0 0 0 0 0 1 x 0 0
0 0 0 0 0 0 0 0 x 0 0
0 0 0 0 0 0 0 1 x 0 0
0 0 0 0 0 0 0 0 x 0 0
0 0 0 0 0 0 0 1 x 0 0
0 0 0 0 0 0 0 0 x 0 0
0 0 0 0 0 0 0 1 x 0 0
0 0 0 0 0 0 0 0 x 0 0
0 0 0 0 0 0 0 1 x 0 0
0 0 0 0 0 0 0 0 x 0 0
0 0 0 0 0 0 0 1 x 0 0
0 0 0 0 0 0 0 0 x 0 0
0 0 0 0 0 0 0 1 x 0 0
0 0 0 0 0 0 0 0 x 0 0
0 0 0 0 0 0 0 1 x 0 0
0 0 0 0 0 0 0 0 x 0 0
0 0 0 0 0 0 0 1 x 0 0
0 0 0 0 0 0 0 0 x 0 0
0 0 0 0 0 0 0 1 x 0 0
0 0 0 0 0 0 0 0 x 0 0
0 0 0 0 0 0 0 1 x 0 0
0 0 0 0 0 0 0 0 x 0 0
0 0 0 0 0 0 0 1 x 0 0
0 0 0 0 0 0 0 0 x 0 0
0 0 0 0 0 0 0 1 x 0 0
0 0 0 0 0 0 0 0 x 0 0
0 0 0 0 0 0 0 1 x 0 0
0 0 0 0 0 0 0 0 x 0 0
0 0 0 0 0 0 0 1 x 0 0
0 0 0 0 0 0 0 0 x 0 0
0 0 0 0 0 0 0 1 x 0 0
0 0 0 0 0 0 0 0 x 0 0
0 0 0 0 0 0 0 1 x 0 0
0 0 0 0 0 0 0 0 x 0 0
0 0 0 0 0 0 0 1 x 0 0
0 0 0 0 0 0 0 0 x 0 0
0 0 0 0 0 0 0 1 x 0 0
0 0 0 0 0 0 0 0 x 0 0
0 0 0 0 0 0 0 1 x 0 0
0 0 0 0 0 0 0 0 x 0 0
0 0 0 0 0 0 0 1 x 0 0
0 0 0 0 0 0 0 0 x 0 0
0 0 0 0 0 0 0 1 x 0 0
0 0 0 0 0 0 0 0 x 0 0
0 0 0 0 0 0 0 1 x 0 0
0 0 0 0 0 0 0 0 x 0 0
0 0 0 0 0 0 0 1 x 0 0
0 0 0 0 0 0 0 0 x 0 0
0 0 0 0 0 0 0 1 x 0 0
0 0 0 0 0 0 0 0 x 0 0
0 0 0 0 0 0 0 1 x 0 0
0 0 0 0 0 0 0 0 x 0 0
0 0 0 0 0 0 0 1 x 0 0
0 0 0 0 0 0 0 0 x 0 0
0 0 0 0 0 0 0 1 x 0 0
0 0 0 0 0 0 0 0 x 0 0
0 0 0 0 0 0 0 1 x 0 0
0 0 0 0 0 0 0 0 x 0 0
0 0 0 0 0 0 0 1 x 0 0
0 0 0 0 0 0 0 0 x 0 0
0 0 0 0 0 0 0 1 x 0 0
0 0 0 0 0 0 0 0 x 0 0
0 0 0 0 0 0 0 1 x 0 0
0 0 0 0 0 0 0 0 x 0 0
0 0 0 0 0 0 0 1 x 0 0
0 0 0 0 0 0 0 0 x 0 0
0 0 0 0 0 0 0 1 x 0 0
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*/

/* Test case 07_P06T01:
M N progIN reset progLoad start result clk valid done output
0 0 0 0 0 0 0 0 x x x
0 0 0 0 0 0 0 1 x x x
0 0 0 1 0 0 0 0 x x x
0 0 0 1 0 0 0 1 0 0 x
0 0 0 0 0 0 0 0 0 0 x
0 0 0 0 0 0 0 1 0 0 x
0 0 0 0 0 0 0 0 0 0 x
0 0 0 0 0 0 0 1 0 0 x
0 0 0 0 0 0 0 0 0 0 x
0 0 0 0 0 0 0 1 0 0 x
0 0 0 0 0 0 0 0 0 0 x
0 0 0 0 0 0 0 1 0 0 x
0 0 0 0 0 0 0 0 0 0 x
0 0 0 0 0 0 0 1 0 0 x
0 0 0 0 0 0 0 0 0 0 x
0 0 0 0 0 0 0 1 0 0 x
0 0 0 0 0 0 0 0 0 0 x
0 0 0 0 0 0 0 1 0 0 x
0 0 0 0 0 0 0 0 0 0 x
0 0 0 0 0 0 0 1 0 0 x
0 0 0 0 0 0 0 0 0 0 x
0 0 0 0 0 0 0 1 0 0 x
0 0 0 0 0 0 0 0 0 0 x
0 0 0 0 0 0 0 1 0 0 x
0 0 0 0 0 0 0 0 0 0 x
0 0 0 0 0 0 0 1 0 0 x
0 0 0 0 0 0 0 0 0 0 x
0 0 0 0 0 0 0 1 0 0 x
0 0 0 0 0 0 0 0 0 0 x
0 0 0 0 0 0 0 1 0 0 x
0 0 0 0 0 0 0 0 0 0 x
0 0 0 0 0 0 0 1 0 0 x
0 0 0 0 0 0 0 0 0 0 x
0 0 0 0 0 0 0 1 0 0 x
0 0 0 0 0 0 0 0 0 0 x
0 0 0 0 0 0 0 1 0 0 x
0 0 0 0 0 0 0 0 0 0 x
0 0 0 0 0 0 0 1 0 0 x
0 0 0 0 0 0 0 0 0 0 x
0 0 0 0 0 0 0 1 0 0 x
0 0 0 0 0 0 0 0 0 0 x
0 0 0 0 0 0 0 1 0 0 x
0 0 1792 0 1 0 0 0 0 0 x
0 0 1792 0 1 0 0 1 0 0 x
0 0 1536 0 1 0 0 0 0 0 x
0 0 1536 0 1 0 0 1 0 0 x
0 0 2817 0 1 0 0 0 0 0 x
0 0 2817 0 1 0 0 1 0 0 x
0 0 2048 0 1 0 0 0 0 0 x
0 0 2048 0 1 0 0 1 0 0 x
0 0 1536 0 1 0 0 0 0 0 x
0 0 1536 0 1 0 0 1 0 0 x
0 0 2818 0 1 0 0 0 0 0 x
0 0 2818 0 1 0 0 1 0 0 x
0 0 1024 0 1 0 0 0 0 0 x
0 0 1024 0 1 0 0 1 0 0 x
0 0 2561 0 1 0 0 0 0 0 x
0 0 2561 0 1 0 0 1 0 0 x
0 0 4864 0 1 0 0 0 0 0 x
0 0 4864 0 1 0 0 1 0 0 x
0 0 2819 0 1 0 0 0 0 0 x
0 0 2819 0 1 0 0 1 0 0 x
0 0 2561 0 1 0 0 0 0 0 x
0 0 2561 0 1 0 0 1 0 0 x
0 0 5120 0 1 0 0 0 0 0 x
0 0 5120 0 1 0 0 1 0 0 x
0 0 2820 0 1 0 0 0 0 0 x
0 0 2820 0 1 0 0 1 0 0 x
0 0 7936 0 1 0 0 0 0 0 x
0 0 7936 0 1 0 0 1 0 0 x
15 7 0 0 0 1 0 0 0 0 x
15 7 0 0 0 1 0 1 0 0 x
15 7 0 0 0 0 0 0 x 0 x
15 7 0 0 0 0 0 1 x 0 x
15 7 0 0 0 0 0 0 x 0 x
15 7 0 0 0 0 0 1 x 0 x
15 7 0 0 0 0 0 0 x 0 x
15 7 0 0 0 0 0 1 x 0 x
15 7 0 0 0 0 0 0 x 0 x
15 7 0 0 0 0 0 1 x 0 x
15 7 0 0 0 0 0 0 x 0 x
15 7 0 0 0 0 0 1 x 0 x
15 7 0 0 0 0 0 0 x 0 x
15 7 0 0 0 0 0 1 x 0 x
15 7 0 0 0 0 0 0 x 0 x
15 7 0 0 0 0 0 1 x 0 x
15 7 0 0 0 0 0 0 x 0 x
15 7 0 0 0 0 0 1 x 0 x
15 7 0 0 0 0 0 0 x 0 x
15 7 0 0 0 0 0 1 x 0 x
15 7 0 0 0 0 0 0 x 0 x
15 7 0 0 0 0 0 1 x 0 x
15 7 0 0 0 0 0 0 x 0 x
15 7 0 0 0 0 0 1 x 0 x
15 7 0 0 0 0 0 0 x 0 x
15 7 0 0 0 0 0 1 x 0 x
15 7 0 0 0 0 0 0 x 0 x
15 7 0 0 0 0 0 1 x 0 x
15 7 0 0 0 0 0 0 x 0 x
15 7 0 0 0 0 0 1 x 0 x
15 7 0 0 0 0 0 0 x 0 x
15 7 0 0 0 0 0 1 x 0 x
15 7 0 0 0 0 0 0 x 0 x
15 7 0 0 0 0 0 1 x 0 x
15 7 0 0 0 0 0 0 x 0 x
15 7 0 0 0 0 0 1 x 0 x
15 7 0 0 0 0 0 0 x 0 x
15 7 0 0 0 0 0 1 x 0 x
15 7 0 0 0 0 0 0 x 0 x
15 7 0 0 0 0 0 1 x 0 x
15 7 0 0 0 0 0 0 x 0 x
0 0 0 0 0 0 0 1 x 0 x
0 0 0 0 0 0 0 0 x 0 x
0 0 0 0 0 0 0 1 x 0 x
0 0 0 0 0 0 0 0 x 0 x
0 0 0 0 0 0 0 1 x 0 x
0 0 0 0 0 0 0 0 x 0 x
0 0 0 0 0 0 0 1 x 0 x
0 0 0 0 0 0 0 0 x 0 x
0 0 0 0 0 0 0 1 x 0 x
0 0 0 0 0 0 0 0 x 0 x
0 0 0 0 0 0 0 1 x 0 x
0 0 0 0 0 0 0 0 x 0 x
0 0 0 0 0 0 0 1 1 0 x
0 0 0 0 0 0 1 0 1 0 0
0 0 0 0 0 0 1 1 1 0 0
0 0 0 0 0 0 0 0 1 0 0
0 0 0 0 0 0 0 1 1 0 15
0 0 0 0 0 0 0 0 1 0 15
0 0 0 0 0 0 0 1 1 0 7
0 0 0 0 0 0 0 0 1 0 7
0 0 0 0 0 0 0 1 1 0 105
0 0 0 0 0 0 0 0 1 0 105
0 0 0 0 0 0 0 1 1 0 2
0 0 0 0 0 0 0 0 1 0 2
0 0 0 0 0 0 0 1 1 0 0
0 0 0 0 0 0 0 0 1 0 0
0 0 0 0 0 0 0 1 1 0 0
0 0 0 0 0 0 0 0 1 0 0
0 0 0 0 0 0 0 1 1 0 0
0 0 0 0 0 0 0 0 1 0 0
0 0 0 0 0 0 0 1 1 0 0
0 0 0 0 0 0 0 0 1 0 0
0 0 0 0 0 0 0 1 1 0 0
0 0 0 0 0 0 0 0 1 0 0
0 0 0 0 0 0 0 1 1 0 0
0 0 0 0 0 0 0 0 1 0 0
0 0 0 0 0 0 0 1 1 0 0
0 0 0 0 0 0 0 0 1 0 0
0 0 0 0 0 0 0 1 1 0 0
0 0 0 0 0 0 0 0 1 0 0
0 0 0 0 0 0 0 1 1 0 0
0 0 0 0 0 0 0 0 1 0 0
0 0 0 0 0 0 0 1 1 0 0
0 0 0 0 0 0 0 0 1 0 0
0 0 0 0 0 0 0 1 1 0 0
0 0 0 0 0 0 0 0 1 0 0
0 0 0 0 0 0 0 1 1 1 x
0 0 0 0 0 0 0 0 1 1 x
0 0 0 0 0 0 0 1 1 1 x
0 0 0 0 0 0 0 0 1 1 x
*/

/* Test case 02_P01T02:
M N progIN reset progLoad start result clk valid done output
0 0 0 0 0 0 0 0 x x x
0 0 0 0 0 0 0 1 x x x
0 0 0 1 0 0 0 0 x x x
0 0 0 1 0 0 0 1 0 0 0
0 0 0 0 0 0 0 0 0 0 0
0 0 0 0 0 0 0 1 0 0 0
0 0 0 0 0 0 0 0 0 0 0
0 0 0 0 0 0 0 1 0 0 0
0 0 0 0 0 0 0 0 0 0 0
0 0 0 0 0 0 0 1 0 0 0
0 0 0 0 0 0 0 0 0 0 0
0 0 0 0 0 0 0 1 0 0 0
0 0 0 0 0 0 0 0 0 0 0
0 0 0 0 0 0 0 1 0 0 0
0 0 0 0 0 0 0 0 0 0 0
0 0 0 0 0 0 0 1 0 0 0
0 0 0 0 0 0 0 0 0 0 0
0 0 0 0 0 0 0 1 0 0 0
0 0 0 0 0 0 0 0 0 0 0
0 0 0 0 0 0 0 1 0 0 0
0 0 0 0 0 0 0 0 0 0 0
0 0 0 0 0 0 0 1 0 0 0
0 0 0 0 0 0 0 0 0 0 0
0 0 0 0 0 0 0 1 0 0 0
0 0 0 0 0 0 0 0 0 0 0
0 0 0 0 0 0 0 1 0 0 0
0 0 0 0 0 0 0 0 0 0 0
0 0 0 0 0 0 0 1 0 0 0
0 0 0 0 0 0 0 0 0 0 0
0 0 0 0 0 0 0 1 0 0 0
0 0 0 0 0 0 0 0 0 0 0
0 0 0 0 0 0 0 1 0 0 0
0 0 0 0 0 0 0 0 0 0 0
0 0 0 0 0 0 0 1 0 0 0
0 0 0 0 0 0 0 0 0 0 0
0 0 0 0 0 0 0 1 0 0 0
0 0 0 0 0 0 0 0 0 0 0
0 0 0 0 0 0 0 1 0 0 0
0 0 0 0 0 0 0 0 0 0 0
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*/

/* Test case 04_P03T01:
M N progIN reset progLoad start result clk valid done output
0 0 0 0 0 0 0 0 x x x
0 0 0 0 0 0 0 1 x x x
0 0 0 1 0 0 0 0 x x x
0 0 0 1 0 0 0 1 0 0 0
0 0 0 0 0 0 0 0 0 0 0
0 0 0 0 0 0 0 1 0 0 0
0 0 0 0 0 0 0 0 0 0 0
0 0 0 0 0 0 0 1 0 0 0
0 0 0 0 0 0 0 0 0 0 0
0 0 0 0 0 0 0 1 0 0 0
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*/

/* Test case 06_P05T1:
M N progIN reset progLoad start result clk valid done output
0 0 0 0 0 0 0 0 x x x
0 0 0 0 0 0 0 1 x x x
0 0 0 1 0 0 0 0 x x x
0 0 0 1 0 0 0 1 0 0 x
0 0 0 0 0 0 0 0 0 0 x
0 0 0 0 0 0 0 1 0 0 x
0 0 0 0 0 0 0 0 0 0 x
0 0 0 0 0 0 0 1 0 0 x
0 0 0 0 0 0 0 0 0 0 x
0 0 0 0 0 0 0 1 0 0 x
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*/

/* Test case 08_P06T02:
M N progIN reset progLoad start result clk valid done output
0 0 0 0 0 0 0 0 x x x
0 0 0 0 0 0 0 1 x x x
0 0 0 1 0 0 0 0 x x x
0 0 0 1 0 0 0 1 0 0 x
0 0 0 0 0 0 0 0 0 0 x
0 0 0 0 0 0 0 1 0 0 x
0 0 0 0 0 0 0 0 0 0 x
0 0 0 0 0 0 0 1 0 0 x
0 0 0 0 0 0 0 0 0 0 x
0 0 0 0 0 0 0 1 0 0 x
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*/
